# Fritzing sketch ESP32 plantSitter (saved by Fritzing 0.9.3b)
breadboards: 1

parts:
  Part1 = FC-28 Soil Hygrometer Module - Probe
  Part2 = FC-28 Soil Hygrometer Module
  Grove1 = Grove OLED 128x96
  Part3 = FC-28 Soil Hygrometer Module - Probe
  Part4 = FC-28 Soil Hygrometer Module
  Part5 = FC-28 Soil Hygrometer Module - Probe
  Part6 = FC-28 Soil Hygrometer Module
  M1 = DOIT Esp32 DevKit v1 (30 pins long, 11 pins width) [part_number=ESP32S-PIN30]
  DHT1 = Humidity and Temperature Sensor DHT22 [part_number=DHT22]
  R1 = Resistor [tolerance=±5% resistance=10k package="0402 [SMD]"]
  S2 = Momentary Switch [package=ksa_sealed_tac_switch]

nets:
  N1: Part1.POS, Part2.POS
  N2: Part1.NEG, Part2.NEG
  N3: Part2.VCC, M1.D25
  GND: Part2.GND, Grove1.GND, Part4.GND, Part6.GND, DHT1.GND_2
  N4: Part2.AO, M1.VP
  VCC: Grove1.VCC, M1.3V3, DHT1.Vcc, R1.Pin_0
  N5: Grove1.SDA, M1.D22
  N6: Grove1.SCL, M1.D21
  N7: Part3.POS, Part4.POS
  N8: Part3.NEG, Part4.NEG
  N9: Part4.VCC, M1.D26
  N10: Part4.AO, M1.D34
  N11: Part5.POS, Part6.POS
  N12: Part5.NEG, Part6.NEG
  N13: Part6.VCC, M1.D27
  N14: Part6.AO, M1.D32
  N15: M1.D15, S2.1
  N16: M1.D4, DHT1.Data-signal, R1.Pin_1

custom parts:
  FC-28 Soil Hygrometer Module - Probe: The FC-28 is a soil hygrometer module that uses the Texas Instruments LM393 comparator chip to provide an analog measurement of soil humidity.
  FC-28 Soil Hygrometer Module: The FC-28 is a soil hygrometer module that uses the Texas Instruments LM393 comparator chip to provide an analog measurement of soil humidity. The digital output is high when soil moisture is over a certain threshold, as determined by adjusting the potentiometer.
  DOIT Esp32 DevKit v1 (30 pins long, 11 pins width): The DOIT Esp32 DevKit v1 is one of the development board created by DOIT to evaluate the ESP-WROOM-32 module. It is based on the ESP32 microcontroller that boasts Wifi, Bluetooth, Ethernet and Low Power support all in a single chip. (vanepp) made breadboard work, adjusted pin numbering and labels and reduced size of schematic and cleaned up pcb. This chip is 30pins long (2 x15) and 11 pins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
  Humidity and Temperature Sensor DHT22: Digital relative humidity & temperature sensor DHT22

// code stored in the sketch: plantSitter.ino
#include <Wire.h>
#include <Adafruit_GFX.h>
#include <Adafruit_SSD1306.h>

#define SCREEN_WIDTH 128 // OLED display width, in pixels
#define SCREEN_HEIGHT 64 // OLED display height, in pixels
// Declaration for an SSD1306 display connected to I2C (SDA, SCL pins)
Adafruit_SSD1306 display(SCREEN_WIDTH, SCREEN_HEIGHT, &Wire, -1);

//soil moisture
/* Change these values based on your calibration values */
#define soilWet 500   // Define max value we consider soil 'wet'
#define soilDry 750   // Define min value we consider soil 'dry'

// Moisture Sensor pins
#define sensorPower 3
// #define sensorPin 4
#define sensorPin A0

//CHANGE THIS TO YOUR PLANT'S NAME
#define plantName "Basilson"

void setup() {
  Serial.begin(9600);

	pinMode(sensorPower, OUTPUT);
  pinMode(sensorPin, INPUT);
	// Initially keep the sensor OFF
	digitalWrite(sensorPower, LOW);
	
  //int SSD1306
	if(!display.begin(SSD1306_SWITCHCAPVCC, 0x3C)) { // Address 0x3D for 128x64
    Serial.println(F("SSD1306 allocation failed"));
    for(;;);
  }
  delay(50);
  display.clearDisplay();

  display.setTextSize(1);
  display.setTextColor(WHITE);
  display.setCursor(0, 10);
  // Display static text
  display.print("Hello, I'm ");
  display.println(plantName);
  display.display(); 
  delay(1000);

}

void loop() {
	//get the reading from the function below and print it
	int moisture = readSensor();
	Serial.print("Current moisture: ");
	Serial.println(moisture);

  String status;
	// Determine status of our soil
	if (moisture < soilWet) {
    status = "I'm Hydrated"; 
		Serial.println(status);

	} else if (moisture >= soilWet && moisture < soilDry) {
    status = "I'm still doing well"; 
		Serial.println(status);
	} else {
		status = "I'm thursty"; 
		Serial.println(status);
	}
	

	// delay(5000);	// Take readings 3 times day, every 8 hours
	// delay(1000);	// Take a reading every second for testing
					// Normally you should take reading perhaps once or twice a day
  // Serial.println("last time watered: ");
  // Serial.println(seconds ago);
  // Serial.println("minutes ago");
  // Serial.println("hours ago");
  // Serial.println("days ago");

  display.clearDisplay();
  display.setTextSize(1);
  display.setTextColor(WHITE);

  display.setCursor(0, 10);
  display.print("Name: ");
  display.println(plantName);

  display.setCursor(0, 20);
  display.print("Current moisture:");
  display.println(moisture);

  display.setCursor(0, 30);
  display.print("Last watered: ");
  display.print("X");
  display.println("d");

  display.setCursor(0, 49);
  display.print("Status: ");
  display.print(status);

  display.display(); 

  delay(5000);
}

//  This function returns the analog soil moisture measurement
int readSensor() {
	digitalWrite(sensorPower, HIGH);	// Turn the sensor ON
	delay(10);							// Allow power to settle
	int val = analogRead(sensorPin);	// Read the analog value form sensor
	digitalWrite(sensorPower, LOW);		// Turn the sensor OFF
	return val;							// Return analog moisture value
}
