# Fritzing sketch Circuit DiagramWifi (saved by Fritzing 0.9.3b)
breadboards: 1

parts:
  Part1 = FC-28 Soil Hygrometer Module - Probe
  Part2 = FC-28 Soil Hygrometer Module
  Grove1 = Grove OLED 128x96
  Part4 = Real Time Clock Module - DS1307 RTC Breakout Board
  esp1 = ESP32 DevKitc V4

nets:
  N1: Part1.POS, Part2.POS
  N2: Part1.NEG, Part2.NEG
  VCC: Part2.VCC, Grove1.VCC, Part4.5V, esp1.5V
  N3: Part2.GND, esp1.GND#32
  N4: Part2.AO, esp1.IO4
  GND: Grove1.GND, Part4.GND, esp1.GND#18
  N5: Grove1.SDA, Part4.SDA, esp1.IO21
  N6: Grove1.SCL, Part4.SCL, esp1.IO22

notes:
  Real Time Counter
  ESP32 Board
  SSD1306 OLED Display
  Soil Moisture Sensor
  Probe & Module
  soil

custom parts:
  FC-28 Soil Hygrometer Module - Probe: The FC-28 is a soil hygrometer module that uses the Texas Instruments LM393 comparator chip to provide an analog measurement of soil humidity.
  FC-28 Soil Hygrometer Module: The FC-28 is a soil hygrometer module that uses the Texas Instruments LM393 comparator chip to provide an analog measurement of soil humidity. The digital output is high when soil moisture is over a certain threshold, as determined by adjusting the potentiometer.
  ESP32 DevKitc V4: ESP32-DevKitC board with ESP32-WROOM-32 module. ESP32-DevKitC V4 is a small-sized ESP32-based development board produced by Espressif. Most of the pins on the ESP module are broken out to the pin headers on the board. The pins D0, D1, D2, D3, CMD and CLK are used internally for communication between ESP32 and SPI flash memory. They are grouped on both sides near the USB connector. Avoid using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

// code stored in the sketch: plantSitter.ino
#include <Wire.h>
#include <Adafruit_GFX.h>
#include <Adafruit_SSD1306.h>

#define SCREEN_WIDTH 128 // OLED display width, in pixels
#define SCREEN_HEIGHT 64 // OLED display height, in pixels
// Declaration for an SSD1306 display connected to I2C (SDA, SCL pins)
Adafruit_SSD1306 display(SCREEN_WIDTH, SCREEN_HEIGHT, &Wire, -1);

//soil moisture
/* Change these values based on your calibration values */
#define soilWet 500   // Define max value we consider soil 'wet'
#define soilDry 750   // Define min value we consider soil 'dry'

// Moisture Sensor pins
#define sensorPower 3
// #define sensorPin 4
#define sensorPin A0

//CHANGE THIS TO YOUR PLANT'S NAME
#define plantName "Basilson"

void setup() {
  Serial.begin(9600);

	pinMode(sensorPower, OUTPUT);
  pinMode(sensorPin, INPUT);
	// Initially keep the sensor OFF
	digitalWrite(sensorPower, LOW);
	
  //int SSD1306
	if(!display.begin(SSD1306_SWITCHCAPVCC, 0x3C)) { // Address 0x3D for 128x64
    Serial.println(F("SSD1306 allocation failed"));
    for(;;);
  }
  delay(50);
  display.clearDisplay();

  display.setTextSize(1);
  display.setTextColor(WHITE);
  display.setCursor(0, 10);
  // Display static text
  display.print("Hello, I'm ");
  display.println(plantName);
  display.display(); 
  delay(1000);

}

void loop() {
	//get the reading from the function below and print it
	int moisture = readSensor();
	Serial.print("Current moisture: ");
	Serial.println(moisture);

  String status;
	// Determine status of our soil
	if (moisture < soilWet) {
    status = "I'm Hydrated"; 
		Serial.println(status);

	} else if (moisture >= soilWet && moisture < soilDry) {
    status = "I'm still doing well"; 
		Serial.println(status);
	} else {
		status = "I'm thursty"; 
		Serial.println(status);
	}
	

	// delay(5000);	// Take readings 3 times day, every 8 hours
	// delay(1000);	// Take a reading every second for testing
					// Normally you should take reading perhaps once or twice a day
  // Serial.println("last time watered: ");
  // Serial.println(seconds ago);
  // Serial.println("minutes ago");
  // Serial.println("hours ago");
  // Serial.println("days ago");

  display.clearDisplay();
  display.setTextSize(1);
  display.setTextColor(WHITE);

  display.setCursor(0, 10);
  display.print("Name: ");
  display.println(plantName);

  display.setCursor(0, 20);
  display.print("Current moisture:");
  display.println(moisture);

  display.setCursor(0, 30);
  display.print("Last watered: ");
  display.print("X");
  display.println("d");

  display.setCursor(0, 49);
  display.print("Status: ");
  display.print(status);

  display.display(); 

  delay(5000);
}

//  This function returns the analog soil moisture measurement
int readSensor() {
	digitalWrite(sensorPower, HIGH);	// Turn the sensor ON
	delay(10);							// Allow power to settle
	int val = analogRead(sensorPin);	// Read the analog value form sensor
	digitalWrite(sensorPower, LOW);		// Turn the sensor OFF
	return val;							// Return analog moisture value
}
